// Logisim project 8-BIT-CPU.circ as structural Verilog: 1 circuit, main circuit 8_BIT_CPU
module _8_BIT_CPU (
  input  _2s_COMP_MODE_SEL,
  input  MANUAL_CLK_PUL,
  input  MANUAL_CLK_SEL,
  input  RESET,
  output [7:0] DISPLAY_REGISTER,
  output [7:0] A_REGISTER,
  output [7:0] BUS_READING,
  output [7:0] B_REGISTER,
  output [7:0] ALU,
  output [3:0] out_10,
  output [2:0] REGISTER,
  output [3:0] REGISTER_2,
  output [7:0] INST__REGISTER,
  output HLT,
  output AI,
  output AO,
  output BI,
  output DO,
  output EO,
  output SU,
  output RI,
  output RO,
  output MI,
  output PI,
  output PO,
  output PE,
  output II,
  output IO,
  output FI
);

  wire and_1_out, and_2_out, and_3_out, and_5_out, CLK_out, not_1_out, not_2_out, not_3_out, not_4_out,
       not_5_out, or_1_out, or_2_out;
  wire [1:0] nor_1_out;
  wire [2:0] counter_2_q;
  wire [3:0] rom_2_data, rom_2_data_2, rom_3_data, rom_3_data_2;
  wire [7:0] bit_extender_1_out, ram_1_data, rom_1_data, undriven, xor_1_out;
  wire [7:4] controlled_buffer_6_out;

  Clock CLK (.out(CLK_out));
  and and_1 (and_1_out, MANUAL_CLK_PUL, MANUAL_CLK_SEL);
  not not_1 (not_1_out, MANUAL_CLK_SEL);
  and and_2 (and_2_out, not_1_out, CLK_out);
  not not_2 (not_2_out, HLT);
  Counter #(.width(4), .max('hf)) counter_1 (
    .load(PI), .D(BUS_READING[3:0]), .count(PE), .Q(out_10), .clk(and_3_out), .clr(RESET));  // open: carry
  or or_1 (or_1_out, and_1_out, and_2_out);
  assign BUS_READING[3:0] = PO ? out_10 : 4'bz;  // Controlled_Buffer controlled_buffer_1
  and and_3 (and_3_out, or_1_out, not_2_out);
  Register #(.width(4)) register_1 (.D(BUS_READING[3:0]), .en(MI), .Q(REGISTER_2), .clk(and_3_out), .clr(RESET));
  Register u_register_2 (.D(BUS_READING), .en(AI), .Q(A_REGISTER), .clk(and_3_out), .clr(RESET));
  Register register_3 (.D(BUS_READING), .en(BI), .Q(B_REGISTER), .clk(and_3_out), .clr(RESET));
  assign BUS_READING = AO ? A_REGISTER : 8'bz;  // Controlled_Buffer controlled_buffer_2
  not not_3 (not_3_out, RI);
  and and_4 (undriven[3], DISPLAY_REGISTER[7], _2s_COMP_MODE_SEL);
  RAM #(.addrWidth(4), .bus("asynch")) ram_1 (
    .addr(REGISTER_2), .data(ram_1_data), .sel(1'b1), .ld(not_3_out), .clr(1'b0));
  assign BUS_READING = RO ? ram_1_data : 8'bz;  // Controlled_Buffer controlled_buffer_3
  ROM #(.addrWidth(9)) rom_1 (.addr({_2s_COMP_MODE_SEL, DISPLAY_REGISTER}), .data(rom_1_data), .sel(1'b1));
  Pull_Resistor pull_resistor_1 (.node(BUS_READING));
  assign bit_extender_1_out = {{7{SU}}, SU};  // Bit_Extender bit_extender_1
  assign ram_1_data = RI ? BUS_READING : 8'bz;  // Controlled_Buffer controlled_buffer_4
  assign xor_1_out = bit_extender_1_out ^ B_REGISTER;  // XOR_Gate xor_1, 8 bits wide
  _7_Segment_Display u_7_segment_display_1 (
    .g(undriven[3]), .f(undriven[2]), .a(undriven[1]), .b(undriven[0]), .e(undriven[4]), .d(undriven[5]),
    .c(undriven[6]), .dp(undriven[7]));
  ROM #(.addrWidth(9)) rom_2 (
    .addr({_2s_COMP_MODE_SEL, DISPLAY_REGISTER}),
    .data({rom_2_data_2[0], rom_2_data_2[1], rom_2_data_2[2], rom_2_data_2[3], rom_2_data}), .sel(1'b1));
  Adder adder_1 (.a(A_REGISTER), .b(xor_1_out), .out(ALU), .cin(SU), .cout(nor_1_out[1]));
  assign BUS_READING = EO ? ALU : 8'bz;  // Controlled_Buffer controlled_buffer_5
  nor nor_1 (nor_1_out[0], ALU[0], ALU[1], ALU[2], ALU[3], ALU[4], ALU[5], ALU[6], ALU[7]);
  Register register_4 (.D(BUS_READING), .en(II), .Q(INST__REGISTER), .clk(and_3_out), .clr(RESET));
  _7_Segment_Display u_7_segment_display_2 (
    .g(rom_1_data[3]), .f(rom_1_data[2]), .a(rom_1_data[1]), .b(rom_1_data[0]), .e(rom_1_data[4]),
    .d(rom_1_data[5]), .c(rom_1_data[6]), .dp(rom_1_data[7]));
  Register #(.width(3)) register_5 (.D({ALU[7], nor_1_out}), .en(FI), .Q(REGISTER), .clk(and_3_out), .clr(RESET));
  assign {controlled_buffer_6_out, BUS_READING[3:0]} = IO ? INST__REGISTER : 8'bz;  // Controlled_Buffer controlled_buffer_6
  _7_Segment_Display u_7_segment_display_3 (
    .g(rom_3_data[3]), .f(rom_3_data[2]), .a(rom_3_data[1]), .b(rom_3_data[0]), .e(rom_3_data_2[3]),
    .d(rom_3_data_2[2]), .c(rom_3_data_2[1]), .dp(rom_3_data_2[0]));
  _7_Segment_Display u_7_segment_display_4 (
    .g(rom_2_data[3]), .f(rom_2_data[2]), .a(rom_2_data[1]), .b(rom_2_data[0]), .e(rom_2_data_2[3]),
    .d(rom_2_data_2[2]), .c(rom_2_data_2[1]), .dp(rom_2_data_2[0]));
  ROM #(.addrWidth(9)) rom_3 (
    .addr({_2s_COMP_MODE_SEL, DISPLAY_REGISTER}),
    .data({rom_3_data_2[0], rom_3_data_2[1], rom_3_data_2[2], rom_3_data_2[3], rom_3_data}), .sel(1'b1));
  Register register_6 (.D(BUS_READING), .en(DO), .Q(DISPLAY_REGISTER), .clk(and_3_out), .clr(RESET));
  not not_4 (not_4_out, and_3_out);
  Counter #(.width(3), .max('h7)) counter_2 (
    .load(1'b0), .Q(counter_2_q), .clk(not_4_out), .clr(or_2_out));  // open: D, count, carry
  or or_2 (or_2_out, RESET, and_5_out);
  not not_5 (not_5_out, counter_2_q[1]);
  ROM #(.addrWidth(10), .dataWidth(16)) rom_4 (
    .addr({REGISTER, INST__REGISTER[7:4], counter_2_q}),
    .data({HLT, AI, AO, BI, DO, EO, SU, RI, RO, MI, PI, PO, PE, II, IO, FI}), .sel(1'b1));
  and and_5 (and_5_out, counter_2_q[0], not_5_out, counter_2_q[2]);

  // Notes on the sheet:
  //   CLOCK MODULE
  //   PROGRAM
  //   COUNTER
  //   MEM. ADDR.
  //   DISPLAY MODULE
  //   RAM MODULE
  //   contents of rom_1 (hex, n*v repeats v):
  //   100*77 100*41 56*3b 100*77 57*41 99*77
  //   CONTROL WORD
  //   contents of rom_2 (hex, n*v repeats v):
  //   10*77 10*41 10*3b 10*6b 10*4d 10*6e 10*7e 10*43 10*7f 10*6f 10*77 10*41 10*3b 10*6b 10*4d 10*6e
  //   10*7e 10*43 10*7f 10*6f 10*77 10*41 10*3b 10*6b 10*4d 6*6e 10*77 10*41 10*3b 10*6b 10*4d 10*6e 10*7e
  //   10*43 10*7f 10*6f 10*77 10*41 17*3b 10*41 10*77 10*6f 10*7f 10*43 10*7e 10*6e 10*4d 10*6b 10*3b
  //   10*41 9*77
  //   CPU FLAGS
  //   contents of rom_3 (hex, n*v repeats v):
  //   77 41 3b 6b 4d 6e 7e 43 7f 6f 77 41 3b 6b 4d 6e 7e 43 7f 6f 77 41 3b 6b 4d 6e 7e 43 7f 6f 77 41 3b
  //   6b 4d 6e 7e 43 7f 6f 77 41 3b 6b 4d 6e 7e 43 7f 6f 77 41 3b 6b 4d 6e 7e 43 7f 6f 77 41 3b 6b 4d 6e
  //   7e 43 7f 6f 77 41 3b 6b 4d 6e 7e 43 7f 6f 77 41 3b 6b 4d 6e 7e 43 7f 6f 77 41 3b 6b 4d 6e 7e 43 7f
  //   6f 77 41 3b 6b 4d 6e 7e 43 7f 6f 77 41 3b 6b 4d 6e 7e 43 7f 6f 77 41 3b 6b 4d 6e 7e 43 7f 6f 77 41
  //   3b 6b 4d 6e 7e 43 7f 6f 77 41 3b 6b 4d 6e 7e 43 7f 6f 77 41 3b 6b 4d 6e 7e 43 7f 6f 77 41 3b 6b 4d
  //   6e 7e 43 7f 6f 77 41 3b 6b 4d 6e 7e 43 7f 6f 77 41 3b 6b 4d 6e 7e 43 7f 6f 77 41 3b 6b 4d 6e 7e 43
  //   7f 6f 77 41 3b 6b 4d 6e 7e 43 7f 6f 77 41 3b 6b 4d 6e 7e 43 7f 6f 77 41 3b 6b 4d 6e 7e 43 7f 6f 77
  //   41 3b 6b 4d 6e 7e 43 7f 6f 77 41 3b 6b 4d 6e 7e 43 7f 6f 77 41 3b 6b 4d 6e 77 41 3b 6b 4d 6e 7e 43
  //   7f 6f 77 41 3b 6b 4d 6e 7e 43 7f 6f 77 41 3b 6b 4d 6e 7e 43 7f 6f 77 41 3b 6b 4d 6e 7e 43 7f 6f 77
  //   41 3b 6b 4d 6e 7e 43 7f 6f 77 41 3b 6b 4d 6e 7e 43 7f 6f 77 41 3b 6b 4d 6e 7e 43 7f 6f 77 41 3b 6b
  //   4d 6e 7e 43 7f 6f 77 41 3b 6b 4d 6e 7e 43 7f 6f 77 41 3b 6b 4d 6e 7e 43 7f 6f 77 41 3b 6b 4d 6e 7e
  //   43 7f 6f 77 41 3b 6b 4d 6e 7e 43 7f 6f 77 41 3b 6b 4d 6e 7e 43 7f 43 7e 6e 4d 6b 3b 41 77 6f 7f 43
  //   7e 6e 4d 6b 3b 41 77 6f 7f 43 7e 6e 4d 6b 3b 41 77 6f 7f 43 7e 6e 4d 6b 3b 41 77 6f 7f 43 7e 6e 4d
  //   6b 3b 41 77 6f 7f 43 7e 6e 4d 6b 3b 41 77 6f 7f 43 7e 6e 4d 6b 3b 41 77 6f 7f 43 7e 6e 4d 6b 3b 41
  //   77 6f 7f 43 7e 6e 4d 6b 3b 41 77 6f 7f 43 7e 6e 4d 6b 3b 41 77 6f 7f 43 7e 6e 4d 6b 3b 41 77 6f 7f
  //   43 7e 6e 4d 6b 3b 41 77 6f 7f 43 7e 6e 4d 6b 3b 41
  //   INSTRUCTION DECODER
  //   CONTROL UNIT
  //   MICRO-INST STEP
  //   COUNTER
  //   contents of rom_4 (hex, n*v repeats v):
  //   50 8c 6*0 50 8c 4002 5*0 50 8c 42 4080 4*0 50 8c 42 2100 4*0 50 8c 42 1080 4401 0 0 0 50 8c 42 1080
  //   4601 0 0 0 50 8c 8000 5*0 50 8c 22 5*0 50 8c 6*0 50 8c 6*0 50 8c 6*0 50 8c 6*0 50 8c 2800 37*0 50 8c
  //   4002 5*0 50 8c 42 4080 4*0 50 8c 42 2100 4*0 50 8c 42 1080 4401 0 0 0 50 8c 42 1080 4601 0 0 0 50 8c
  //   8000 5*0 50 8c 22 5*0 50 8c 6*0 50 8c 6*0 50 8c 22 5*0 50 8c 6*0 50 8c 2800 37*0 50 8c 4002 5*0 50
  //   8c 42 4080 4*0 50 8c 42 2100 4*0 50 8c 42 1080 4401 0 0 0 50 8c 42 1080 4601 0 0 0 50 8c 8000 5*0 50
  //   8c 22 5*0 50 8c 6*0 50 8c 22 5*0 50 8c 6*0 50 8c 6*0 50 8c 2800 37*0 50 8c 4002 5*0 50 8c 42 4080
  //   4*0 50 8c 42 2100 4*0 50 8c 42 1080 4401 0 0 0 50 8c 42 1080 4601 0 0 0 50 8c 8000 5*0 50 8c 22 5*0
  //   50 8c 6*0 50 8c 22 5*0 50 8c 22 5*0 50 8c 6*0 50 8c 2800 37*0 50 8c 4002 5*0 50 8c 42 4080 4*0 50 8c
  //   42 2100 4*0 50 8c 42 1080 4401 0 0 0 50 8c 42 1080 4601 0 0 0 50 8c 8000 5*0 50 8c 22 5*0 50 8c 6*0
  //   50 8c 6*0 50 8c 6*0 50 8c 22 5*0 50 8c 2800 37*0 50 8c 4002 5*0 50 8c 42 4080 4*0 50 8c 42 2100 4*0
  //   50 8c 42 1080 4401 0 0 0 50 8c 42 1080 4601 0 0 0 50 8c 8000 5*0 50 8c 22 5*0 50 8c 6*0 50 8c 6*0 50
  //   8c 22 5*0 50 8c 22 5*0 50 8c 2800 37*0 50 8c 4002 5*0 50 8c 42 4080 4*0 50 8c 42 2100 4*0 50 8c 42
  //   1080 4401 0 0 0 50 8c 42 1080 4601 0 0 0 50 8c 8000 5*0 50 8c 22 5*0 50 8c 6*0 50 8c 22 5*0 50 8c
  //   6*0 50 8c 22 5*0 50 8c 2800 37*0 50 8c 4002 5*0 50 8c 42 4080 4*0 50 8c 42 2100 4*0 50 8c 42 1080
  //   4401 0 0 0 50 8c 42 1080 4601 0 0 0 50 8c 8000 5*0 50 8c 22 5*0 50 8c 6*0 50 8c 22 5*0 50 8c 22 5*0
  //   50 8c 22 5*0 50 8c 2800
endmodule
